// Logisim project modelo_banco_registradores.circ as structural Verilog: 6 circuits, main circuit Bloco_Registradores
module Bloco_Registradores (
  input  [15:0] Data_in,
  input  Load,
  input  [15:0] Address_A_OUT,
  input  [1:0] Address_A,
  input  [1:0] Data_address,
  input  [15:0] Address_B_OUT,
  input  [1:0] Address_B,
  input  Clock
);

  wire and_1_out, and_2_out, and_3_out, decoder_1_out0, decoder_1_out1, decoder_1_out2;
  wire [15:0] R1_q, R2_q, R3_q;

  Decoder #(.select(2)) decoder_1 (
    .out0(decoder_1_out0), .out1(decoder_1_out1), .out2(decoder_1_out2), .sel(Data_address));  // open: out3, en
  Register #(.width(16)) R1 (.D(Data_in), .en(and_1_out), .clk(Clock), .Q(R1_q), .clr(1'b0));
  and and_1 (and_1_out, Load, decoder_1_out0);
  Register #(.width(16)) R2 (.D(Data_in), .en(and_2_out), .clk(Clock), .Q(R2_q), .clr(1'b0));
  and and_2 (and_2_out, Load, decoder_1_out1);
  Register #(.width(16)) R3 (.D(Data_in), .en(and_3_out), .clk(Clock), .Q(R3_q), .clr(1'b0));
  and and_3 (and_3_out, Load, decoder_1_out2);
  Multiplexer #(.select(2), .width(16)) multiplexer_1 (
    .in0({16{1'b0}}), .in1(R1_q), .in2(R2_q), .in3(R3_q), .out(Address_A_OUT), .sel(Address_A));
  Multiplexer #(.select(2), .width(16)) multiplexer_2 (
    .in0({16{1'b0}}), .in1(R1_q), .in2(R2_q), .in3(R3_q), .out(Address_B_OUT), .sel(Address_B));

  // Notes on the sheet:
  //   Data_in: initial=0x1
  //   R0
endmodule

module ULA (
  input  [15:0] Operando_A,
  input  [15:0] Resultado_ULA,
  input  [15:0] Operando_B
);

  Adder #(.width(16)) adder_1 (.a(Operando_A), .b(Operando_B), .out(Resultado_ULA));  // open: cin, cout
endmodule

module CPU_Principal (
  input  Clock,
  input  Reset_Global
);

  wire unidade_de_controle_1_load, unidade_de_controle_1_mem_to_reg, unidade_de_controle_1_ula_src;
  wire [1:0] clock_marcelo_1_opcode, clock_marcelo_1_rd, clock_marcelo_1_rs1, clock_marcelo_1_rs2;
  wire [7:0] clock_marcelo_1_imediato;
  wire [15:0] bit_extender_1_out, multiplexer_1_out, multiplexer_2_out, undriven, undriven_2, undriven_3;

  Multiplexer #(.width(16)) multiplexer_1 (
    .in0(undriven), .out(multiplexer_1_out), .sel(unidade_de_controle_1_mem_to_reg));  // open: in1
  clock_marcelo clock_marcelo_1 (
    .Clock(Clock), .Reset(Reset_Global), .Opcode(clock_marcelo_1_opcode), .RD(clock_marcelo_1_rd),
    .RS1(clock_marcelo_1_rs1), .RS2(clock_marcelo_1_rs2), .Imediato(clock_marcelo_1_imediato));
  Bloco_Registradores bloco_registradores_1 (
    .Data_in(multiplexer_1_out), .Load(unidade_de_controle_1_load), .Address_A_OUT(undriven_2),
    .Address_A(clock_marcelo_1_rs1), .Data_address(clock_marcelo_1_rd), .Address_B_OUT(undriven_3),
    .Address_B(clock_marcelo_1_rs2), .Clock(Clock));
  assign bit_extender_1_out = {{8{clock_marcelo_1_imediato[7]}}, clock_marcelo_1_imediato};  // Bit_Extender bit_extender_1
  Multiplexer #(.width(16)) multiplexer_2 (
    .in0(undriven_3), .in1(bit_extender_1_out), .out(multiplexer_2_out), .sel(unidade_de_controle_1_ula_src));
  Unidade_de_Controle unidade_de_controle_1 (
    .Opcode(clock_marcelo_1_opcode), .Mem_to_Reg(unidade_de_controle_1_mem_to_reg),
    .Load(unidade_de_controle_1_load), .ULA_Src(unidade_de_controle_1_ula_src));  // open: MemWrite
  ULA ula_1 (.Operando_A(undriven_2), .Resultado_ULA(undriven), .Operando_B(multiplexer_2_out));
endmodule

module Unidade_de_Controle (
  input  [1:0] Opcode,
  output Mem_to_Reg,
  output MemWrite,
  output Load,
  output ULA_Src
);

  wire decoder_1_out2;

  Decoder #(.select(2)) decoder_1 (
    .out0(Mem_to_Reg), .out1(MemWrite), .out2(decoder_1_out2), .sel(Opcode), .en(1'b1));  // open: out3
  or or_1 (Load, Mem_to_Reg, decoder_1_out2);
  or or_2 (ULA_Src, Mem_to_Reg, MemWrite);
endmodule

module Memorias_IR_Murilo (
  input  [4:0] PC_Address,
  input  Clock,
  input  Reset,
  input  [4:0] Data_Address,
  input  MemWrite,
  input  [15:0] Data_Write,
  output [1:0] Opcode,
  output [1:0] RD_RS2,
  output [1:0] RS1,
  output [1:0] RS2,
  output [7:0] Immediate,
  output [15:0] Instruction_IR,
  output [15:0] Data_Read
);

  wire [15:0] Instruction_Memory_data;

  ROM #(.addrWidth(5), .dataWidth(16)) Instruction_Memory (.addr(PC_Address), .data(Instruction_Memory_data));
  RAM #(.addrWidth(5), .asyncread("true"), .dataWidth(16), .databus("bibus"), .\type ("nonvolatile")) Data_Memory (
    .addr(Data_Address), .we(MemWrite), .oe(1'b1), .clk(Clock), .din(Data_Write), .dout(Data_Read));
  Register #(.width(16)) IR (
    .D(Instruction_Memory_data), .en(1'b1), .clk(Clock), .Q({Instruction_IR[15:8], Immediate}), .clr(Reset));

  assign Instruction_IR[7:0] = Immediate;
  assign Opcode = Instruction_IR[15:14];
  assign RD_RS2 = Instruction_IR[13:12];
  assign RS1 = Instruction_IR[11:10];
  assign RS2 = Instruction_IR[9:8];

  // Notes on the sheet:
  //   MEMORIA DE INSTRUCOES 32 x 16
  //   contents of Instruction_Memory (hex, n*v repeats v):
  //   100a 200b b600 700c
  //   ROM: 100A 200B B600 700C
  //   MEMORIA DE DADOS 32 x 16
  //   Teste: inicializar Mem[10] = 7 e Mem[11] = 5
  //   IR E DECODIFICACAO DOS CAMPOS
endmodule

module clock_marcelo (
  input  Clock,
  input  Reset,
  output [1:0] Opcode,
  output [1:0] RD,
  output [1:0] RS1,
  output [1:0] RS2,
  output [7:0] Imediato
);

  wire [4:0] adder_1_out, PC_q;
  wire [15:0] undriven;

  Register #(.width(5)) PC (.D(adder_1_out), .clk(Clock), .Q(PC_q), .clr(Reset));  // open: en
  Adder #(.width(5)) adder_1 (.a(PC_q), .b(5'b00001), .out(adder_1_out));  // open: cin, cout
  RAM #(.addrWidth(5), .asyncread("true"), .dataWidth(16), .databus("bidir")) Instruction_Memory (
    .addr(PC_q), .we(1'b0), .oe(1'b1));  // open: clk, data
  Register #(.width(16)) IR (.D(undriven), .Q({Opcode, RD, RS1, RS2, Imediato}), .clk(Clock));  // open: en, clr
endmodule
