// Logisim project trabalho_arquitetura_marcelo.circ as structural Verilog: 1 circuit, main circuit main
module main (
);

  wire clk_out, reset_out;
  wire [4:0] adder_1_out, PC_q;
  wire [15:0] IR_q, undriven;

  Clock clk (.out(clk_out));
  Button reset (.out(reset_out));
  Register #(.width(5)) PC (.D(adder_1_out), .clk(clk_out), .Q(PC_q), .clr(reset_out));  // open: en
  Adder #(.width(5)) adder_1 (.a(PC_q), .b(5'b00001), .out(adder_1_out));  // open: cin, cout
  RAM #(.addrWidth(5), .asyncread("true"), .dataWidth(16), .databus("bidir")) Instruction_Memory (
    .addr(PC_q), .we(1'b0), .oe(1'b1));  // open: clk, data
  Register #(.width(16)) IR (.D(undriven), .Q(IR_q), .clk(clk_out));  // open: en, clr
  // Probe on IR_q[15:14]
  // Probe on IR_q[13:12]
  // Probe on IR_q[11:10]
  // Probe on IR_q[9:8]
  // Probe on IR_q[7:0]
endmodule
